// Logisim project Semisumador.circ as structural Verilog: 1 circuit, main circuit Semisumador
module Semisumador (
  input  in_1,
  input  in_2,
  output out_3,
  output out_4
);

  xor xor_1 (out_3, in_1, in_2);
  and and_1 (out_4, in_1, in_2, in_2);
endmodule
