// Logisim project Sumador.circ as structural Verilog: 1 circuit, main circuit main
module main (
  input  in_1,
  input  in_2,
  output out_3,
  output out_4
);

  wire semisumador_1_out_3, semisumador_1_out_4, semisumador_2_out_4;

  Semisumador semisumador_1 (.in_1(in_1), .in_2(in_2), .out_3(semisumador_1_out_3), .out_4(semisumador_1_out_4));
  Semisumador semisumador_2 (.in_1(semisumador_1_out_3), .in_2(in_2), .out_3(out_3), .out_4(semisumador_2_out_4));
  or or_1 (out_4, semisumador_2_out_4, semisumador_1_out_4);
endmodule
