// Logisim project Sumador8.circ as structural Verilog: 1 circuit, main circuit main
module main (
  input  [7:0] in_1,
  input  [7:0] in_2
);

  Sumador_main main_1 (.in_1(in_1[0]), .in_2(in_2[0]));  // open: out_3, out_4
  Sumador_main main_2 (.in_1(in_1[4]), .in_2(in_2[4]));  // open: out_3, out_4
  Sumador_main main_3 (.in_1(in_1[1]), .in_2(in_2[1]));  // open: out_3, out_4
  Sumador_main main_4 (.in_1(in_1[5]), .in_2(in_1[5]));  // open: out_3, out_4
  Sumador_main main_5 (.in_1(in_1[6]), .in_2(in_2[6]));  // open: out_3, out_4
  Sumador_main main_6 (.in_1(in_1[2]), .in_2(in_2[2]));  // open: out_3, out_4
  Sumador_main main_7 (.in_1(in_1[3]), .in_2(in_2[3]));  // open: out_3, out_4
  Sumador_main main_8 (.in_1(in_1[7]), .in_2(in_2[7]));  // open: out_3, out_4

  assign in_2[5] = in_1[5];
endmodule
